# Fritzing sketch sketch (saved by Fritzing 0.9.2b)
breadboards: 1

parts:
  Raspberry_Pi1 = Raspberry Pi B+  # not connected
  IC1 = MCP3008 8-channel 10-bit ADC [part_number=MCP3008]
  R1 = Photocell (LDR) [package=THT]
  R2 = Resistor [tolerance=±5% resistance=1k package=THT]
  J1 = T Cobbler Plus

nets:
  N1: IC1.no_name_yet#1, R1.pin_1
  N2: IC1.no_name_yet#2, IC1.no_name_yet#3, IC1.no_name_yet#4, IC1.no_name_yet#5, IC1.no_name_yet#6, IC1.no_name_yet#7, IC1.no_name_yet#8, IC1.no_name_yet#9, IC1.no_name_yet#14, J1.GND#5
  N3: IC1.no_name_yet#10, J1.#22
  N4: IC1.no_name_yet#11, J1.#18
  N5: IC1.no_name_yet#12, J1.#16
  N6: IC1.no_name_yet#13, J1.#12
  N7: IC1.no_name_yet#15, IC1.no_name_yet#16, R2.Pin_0, J1.3V3
  N8: R1.pin_0, R2.Pin_1

custom parts:
  T Cobbler Plus: The T-Cobbler Plus is an add on prototyping board from Adafruit specifically designed for the Raspberry Pi B+ that can break out all those tasty power, GPIO, I2C and SPI pins from the 40-pin header onto a solderless breadboard. This set will make "cobbling together" prototypes with the Pi super easy. The T-Cobbler Plus can plug into any solderless breadboard.
